// Logisim project circuitos.circ as structural Verilog
module half_adder (
  input  A,
  input  B,
  output sum,
  output cout
);

  xor xor_1 (sum, A, B);
  and and_1 (cout, A, B);
endmodule

module full_adder (
  input  A,
  input  B,
  input  C,
  output sum,
  output cout
);

  wire half_adder_1_cout, half_adder_1_sum, half_adder_2_cout;

  half_adder half_adder_1 (.A(A), .B(B), .sum(half_adder_1_sum), .cout(half_adder_1_cout));
  half_adder half_adder_2 (.A(half_adder_1_sum), .B(C), .sum(sum), .cout(half_adder_2_cout));
  or or_1 (cout, half_adder_2_cout, half_adder_1_cout);
endmodule
