// Logisim project ep02.circ as structural Verilog: 2 circuits, main circuit 1bit_ula
module _1bit_ula (
  input  Cin,
  input  [1:0] op,
  input  binvert,
  input  A,
  input  B,
  output s,
  output Cout
);

  wire adder_1_out, and_1_out, binvert_1_s, not_1_out, not_2_out, or_1_out;

  binvert binvert_1 (.a(B), .b(not_1_out), .switch(binvert), .s(binvert_1_s));
  not not_1 (not_1_out, B);
  and and_1 (and_1_out, A, binvert_1_s);
  or or_1 (or_1_out, A, binvert_1_s);
  not not_2 (not_2_out, A);
  Adder #(.width(1)) adder_1 (.a(A), .b(binvert_1_s), .out(adder_1_out), .cin(Cin), .cout(Cout));
  Multiplexer #(.select(2), .enable("false")) multiplexer_1 (
    .in0(and_1_out), .in1(or_1_out), .in2(not_2_out), .in3(adder_1_out), .out(s), .sel(op));
endmodule

module binvert (
  input  switch,
  input  a,
  input  b,
  output s
);

  wire and_1_out, and_2_out, not_1_out;

  not not_1 (not_1_out, switch);
  and and_1 (and_1_out, a, not_1_out);
  and and_2 (and_2_out, b, switch);
  or or_1 (s, and_1_out, and_2_out);
endmodule
